// Logisim project Project2Part1.circ as structural Verilog: 1 circuit, main circuit main
module main (
);

  wire and_1_out, and_2_out, and_3_out, and_4_out, and_5_out, and_6_out, clock_1_out, j_k_ff_1_q,
       j_k_ff_1_qn, j_k_ff_2_q, j_k_ff_2_qn, j_k_ff_3_q, j_k_ff_3_qn, not_1_out, not_2_out, or_1_out,
       or_2_out, or_3_out, or_4_out, or_5_out;

  and and_1 (and_1_out, j_k_ff_2_q, j_k_ff_3_q);
  or or_1 (or_1_out, j_k_ff_2_q, j_k_ff_3_q);
  Clock clock_1 (.out(clock_1_out));
  J_K_Flip_Flop j_k_ff_1 (
    .J(and_1_out), .clk(clock_1_out), .K(or_1_out), .Q(j_k_ff_1_q), .Qn(j_k_ff_1_qn));  // open: preset, en, reset
  and and_2 (and_2_out, j_k_ff_1_qn, j_k_ff_3_q);
  or or_2 (or_2_out, j_k_ff_1_q, j_k_ff_3_q);
  J_K_Flip_Flop j_k_ff_2 (
    .J(and_2_out), .clk(clock_1_out), .K(or_2_out), .Q(j_k_ff_2_q), .Qn(j_k_ff_2_qn));  // open: preset, en, reset
  or or_3 (or_3_out, j_k_ff_2_qn, j_k_ff_1_qn);
  J_K_Flip_Flop j_k_ff_3 (
    .J(or_3_out), .clk(clock_1_out), .K(1'b1), .Q(j_k_ff_3_q), .Qn(j_k_ff_3_qn));  // open: preset, en, reset
  and and_3 (and_3_out, j_k_ff_1_q, j_k_ff_2_qn, j_k_ff_3_qn);
  and and_4 (and_4_out, j_k_ff_1_q, j_k_ff_2_qn, j_k_ff_3_q);
  and and_5 (and_5_out, j_k_ff_1_qn, j_k_ff_2_qn, j_k_ff_3_q);
  and and_6 (and_6_out, j_k_ff_1_qn, j_k_ff_2_q, j_k_ff_3_qn);
  or or_4 (or_4_out, and_3_out, and_4_out);
  not not_1 (not_1_out, or_4_out);
  not not_2 (not_2_out, or_5_out);
  or or_5 (or_5_out, and_5_out, and_6_out);
  LED led_1 (.in(not_1_out));
  LED led_2 (.in(and_3_out));
  LED led_3 (.in(and_4_out));
  LED led_4 (.in(and_5_out));
  LED led_5 (.in(and_6_out));
  LED led_6 (.in(not_2_out));

  // Notes on the sheet:
  //   CLK
  //   CLK
  //   CLK
  //   +V
  //   CLK
  //   R1
  //   G1
  //   Y1
  //   G2
  //   Y2
  //   R2
endmodule
