// Logisim project Project2Part2.circ as structural Verilog: 1 circuit, main circuit main
module main (
);

  wire and_1_out, and_2_out, clock_1_out, j_k_ff_1_q, j_k_ff_1_qn, j_k_ff_2_q, j_k_ff_2_qn, not_1_out,
       not_2_out;

  Clock clock_1 (.out(clock_1_out));
  J_K_Flip_Flop j_k_ff_1 (
    .J(j_k_ff_2_q), .clk(clock_1_out), .K(j_k_ff_2_q), .Q(j_k_ff_1_q), .Qn(j_k_ff_1_qn));  // open: preset, en, reset
  J_K_Flip_Flop j_k_ff_2 (
    .J(1'b1), .clk(clock_1_out), .K(1'b1), .Q(j_k_ff_2_q), .Qn(j_k_ff_2_qn));  // open: preset, en, reset
  and and_1 (and_1_out, j_k_ff_1_qn, j_k_ff_2_qn);
  and and_2 (and_2_out, j_k_ff_1_q, j_k_ff_2_qn);
  LED led_1 (.in(and_1_out));
  LED led_2 (.in(not_1_out));
  not not_1 (not_1_out, and_1_out);
  LED led_3 (.in(and_2_out));
  not not_2 (not_2_out, and_2_out);
  LED led_4 (.in(not_2_out));

  // Notes on the sheet:
  //   CLK
  //   CLK
  //   + V
  //   CLK
  //   G1
  //   R1
  //   G2
  //   R2
endmodule
